// Logisim project cpu.circ as structural Verilog: 4 circuits, main circuit CPU
module CPU (
);

  Clock clk ();  // open: out
  Button reset ();  // open: out
  Register #(.width(16)) PC ();  // open: D, en, clk, Q, clr
  ROM #(.addrWidth(16), .dataWidth(16)) rom_1 ();  // open: addr, data
  RegisterFile registerfile_1 ();  // open: Addr_A, Addr_B, Addr_C, we, clk, reset, C, A, B
  Register #(.width(16)) IR ();  // open: D, en, clk, Q, clr
  ALU alu_1 ();  // open: fun, A, B, carry, C, zero, negative, overflow
endmodule

module ALU (
  input  [2:0] fun,
  input  [15:0] A,
  input  [15:0] B,
  output carry,
  output [15:0] C,
  output zero,
  output negative,
  output overflow
);

  wire and_2_out, and_3_out, not_2_out, not_3_out, not_4_out;
  wire [15:0] adder_1_out, and_1_out, multiplexer_1_out, negator_1_out, not_1_out, or_1_out, shifter_1_out,
       shifter_2_out, shifter_3_out;

  Negator #(.width(16)) negator_1 (.in(B), .out(negator_1_out));
  Multiplexer #(.width(16)) multiplexer_1 (.in0(B), .in1(negator_1_out), .out(multiplexer_1_out), .sel(fun[0]));
  assign and_1_out = A & B;  // AND_Gate and_1, 16 bits wide
  assign or_1_out = A | B;  // OR_Gate or_1, 16 bits wide
  Shifter #(.width(16)) shifter_1 (.in(B), .\dist (A[3:0]), .out(shifter_1_out));
  Shifter #(.shift("lr"), .width(16)) shifter_2 (.in(B), .\dist (A[3:0]), .out(shifter_2_out));
  Shifter #(.shift("ar"), .width(16)) shifter_3 (.in(B), .\dist (A[3:0]), .out(shifter_3_out));
  Adder #(.width(16)) adder_1 (.a(A), .b(multiplexer_1_out), .out(adder_1_out), .cin(1'b0), .cout(carry));
  assign not_1_out = ~or_1_out;  // NOT_Gate not_1, 16 bits wide
  not not_2 (not_2_out, multiplexer_1_out[15]);
  not not_3 (not_3_out, B[15]);
  and and_2 (and_2_out, not_2_out, not_3_out, adder_1_out[15]);
  and and_3 (and_3_out, B[15], multiplexer_1_out[15], not_4_out);
  not not_4 (not_4_out, adder_1_out[15]);
  Multiplexer #(.select(3), .width(16)) multiplexer_2 (
    .in0(adder_1_out), .in1(adder_1_out), .in2(and_1_out), .in3(or_1_out), .in4(not_1_out),
    .in5(shifter_1_out), .in6(shifter_2_out), .in7(shifter_3_out), .out(C), .sel(fun));
  or or_2 (overflow, and_2_out, and_3_out);
  Comparator #(.width(16)) comparator_1 (.a(C), .b({16{1'b0}}), .eq(zero), .lt(negative));  // open: gt
endmodule

module RegisterFile (
  input  [2:0] Addr_A,
  input  [2:0] Addr_B,
  input  [2:0] Addr_C,
  input  we,
  input  clk,
  input  reset,
  input  [15:0] C,
  output [15:0] A,
  output [15:0] B
);
endmodule

module RegisterFileTester (
  output halt,
  output [15:0] A,
  output [15:0] B,
  output clk
);

  wire undriven;
  wire [2:0] Addr_A_data, Addr_B_data, Addr_C_data;
  wire [3:0] adder_1_out, addr_q;
  wire [15:0] C_data;

  Clock clock_1 (.out(clk));
  ROM #(.addrWidth(4), .dataWidth(3)) Addr_A (.addr(addr_q), .data(Addr_A_data));
  ROM #(.addrWidth(4), .dataWidth(3)) Addr_B (.addr(addr_q), .data(Addr_B_data));
  ROM #(.addrWidth(4), .dataWidth(3)) Addr_C (.addr(addr_q), .data(Addr_C_data));
  ROM #(.addrWidth(4), .dataWidth(1)) we (.addr(addr_q));  // open: data
  ROM #(.addrWidth(4), .dataWidth(16)) C (.addr(addr_q), .data(C_data));
  Adder #(.width(4)) adder_1 (.a(addr_q), .b(4'b0001), .out(adder_1_out), .cin(1'b0));  // open: cout
  Register #(.width(4)) addr (.D(adder_1_out), .en(1'b1), .clk(clk), .Q(addr_q), .clr(1'b0));
  Comparator #(.width(4)) comparator_1 (.a(addr_q), .b(4'b1111), .eq(halt));  // open: gt, lt
  RegisterFile registerfile_1 (
    .Addr_A(Addr_A_data), .Addr_B(Addr_B_data), .Addr_C(Addr_C_data), .we(undriven), .clk(clk), .reset(1'b0),
    .C(C_data), .A(A), .B(B));

  // Notes on the sheet:
  //   contents of Addr_A (hex, n*v repeats v):
  //   5 2 7 3 2 0 2 6 2 4 1 3 5 5 2 6
  //   contents of Addr_B (hex, n*v repeats v):
  //   4 4 6 0 2 3 5 5 5 0 0 4 5 3 7 5
  //   contents of Addr_C (hex, n*v repeats v):
  //   0 5 0 5 5 7 2 3 6 4 0 4 7 7 4 6
  //   contents of we (hex, n*v repeats v):
  //   0 0 0 1 0 0 1 0 0 0 1 1 0 0 1 1
  //   contents of C (hex, n*v repeats v):
  //   1 4 c f 0 5 9 7 c b 9 f b 9 1 e
endmodule
